# Fritzing sketch DAC_Teensy (saved by Fritzing 0.9.3b)
circuit board: 8.46667cm x 5.64444cm
breadboards: 1

parts:
  Bauteil1 = Thumb Joystick
  C1 = Capacitor [package=cap-pth-small-kit]
  R1 = Resistor [tolerance=±5% resistance=10k package="0402 [SMD]"]
  Teensy_3_1 = Teensy 3.1
  J1 = Dagu DGServo 9g header (male) [package=THT]
  MCP1 = MCP4922 [package="DIP (Dual Inline) [THT]"]

nets (from the breadboard view):
  GND: Bauteil1.GND, C1.2, Teensy_3_1.GND, J1.GND, MCP1.LDAC, MCP1.AV_SS
  N1: Bauteil1.SEL, R1.Pin_1, Teensy_3_1.A0/D14
  N2: Bauteil1.HORZ, Teensy_3_1.A3/D17
  N3: Bauteil1.VERT, Teensy_3_1.A4/D18
  VCC: Bauteil1.VCC, C1.1, R1.Pin_0, Teensy_3_1.Vin, MCP1.VDD, MCP1.SHDN, MCP1.VREF_B, MCP1.VREF_A
  N4: Teensy_3_1.D6, MCP1.CS
  N5: Teensy_3_1.D11, MCP1.SDI
  N6: Teensy_3_1.D13, MCP1.SCK
  N7: J1.X, MCP1.VOUT_A
  N8: J1.Y, MCP1.VOUT_B

custom parts:
  Teensy 3.1: The Teensy is a complete USB-based microcontoller development system, in a very small footprint, capable of implementing many types of projects. All programming is done via the USB port. No special programmer is needed, only a standard micro-USB cable and a PC or Macintosh with a USB port. It has a USB keyboard/mouse/joystick emulation stack and can be programmed through Arduino IDE.
  Dagu DGServo 9g header (male): Dagu DGServo 9g header (male) This part is a minor variation of the standard three pin header; in schematic view the pins have been labelled to show clearly pulse, Vcc and ground. Plug this header into a breadboard, stripboard or PCB to allow a servo header female connector plug (e.g. on the Dagu DGServo 9g) to be connected to the board.
  MCP4922: A DIP stand-in part for whatever IC you want. With 14 pins on a 300mil dual inline package (DIP) footprint.
